// Logisim project GRF.circ as structural Verilog: 1 circuit, main circuit GRF
module GRF (
  input  [4:0] A1,
  input  clk,
  input  reset,
  input  we,
  input  [4:0] A2,
  input  [4:0] A3,
  input  [31:0] WD,
  output [31:0] RD1,
  output [31:0] RD2
);

  wire [31:0] I0, I1, I2, I3, I4, I5, I6, I7, I8, I9, I10, I11, I12, I13, I14, I15, I16, I17, I18, I19, I20,
       I21, I22, I23, I24, I25, I26, I27, I28, I29, I30, I31, O0, O1, O2, O3, O4, O5, O6, O7, O8, O9, O10,
       O11, O12, O13, O14, O15, O16, O17, O18, O19, O20, O21, O22, O23, O24, O25, O26, O27, O28, O29, O30,
       O31;

  Demultiplexer #(.select(5), .width(32), .tristate("true")) demultiplexer_1 (
    .out0(I0), .out1(I1), .out2(I2), .out3(I3), .out4(I4), .out5(I5), .out6(I6), .out7(I7), .out8(I8),
    .out9(I9), .out10(I10), .out11(I11), .out12(I12), .out13(I13), .out14(I14), .out15(I15), .out16(I16),
    .out17(I17), .out18(I18), .out19(I19), .out20(I20), .out21(I21), .out22(I22), .out23(I23), .out24(I24),
    .out25(I25), .out26(I26), .out27(I27), .out28(I28), .out29(I29), .out30(I30), .out31(I31), .in(WD),
    .sel(A3));  // open: en
  Multiplexer #(.select(5), .width(32)) multiplexer_1 (
    .in0(O0), .in1(O1), .in2(O2), .in3(O3), .in4(O4), .in5(O5), .in6(O6), .in7(O7), .in8(O8), .in9(O9),
    .in10(O10), .in11(O11), .in12(O12), .in13(O13), .in14(O14), .in15(O15), .in16(O16), .in17(O17),
    .in18(O18), .in19(O19), .in20(O20), .in21(O21), .in22(O22), .in23(O23), .in24(O24), .in25(O25),
    .in26(O26), .in27(O27), .in28(O28), .in29(O29), .in30(O30), .in31(O31), .out(RD2), .sel(A2));  // open: en
  Multiplexer #(.select(5), .width(32)) multiplexer_2 (
    .in0(O0), .in1(O1), .in2(O2), .in3(O3), .in4(O4), .in5(O5), .in6(O6), .in7(O7), .in8(O8), .in9(O9),
    .in10(O10), .in11(O11), .in12(O12), .in13(O13), .in14(O14), .in15(O15), .in16(O16), .in17(O17),
    .in18(O18), .in19(O19), .in20(O20), .in21(O21), .in22(O22), .in23(O23), .in24(O24), .in25(O25),
    .in26(O26), .in27(O27), .in28(O28), .in29(O29), .in30(O30), .in31(O31), .out(RD1), .sel(A1));  // open: en
  Register #(.width(32)) register_1 (.D({32{1'b0}}), .en(we), .Q(O0), .clk(clk), .clr(reset));
  Register #(.width(32)) register_2 (.D(I8), .en(we), .Q(O8), .clk(clk), .clr(reset));
  Register #(.width(32)) register_3 (.D(I16), .en(we), .Q(O16), .clk(clk), .clr(reset));
  Register #(.width(32)) register_4 (.D(I24), .en(we), .Q(O24), .clk(clk), .clr(reset));
  Register #(.width(32)) register_5 (.D(I1), .en(we), .Q(O1), .clk(clk), .clr(reset));
  Register #(.width(32)) register_6 (.D(I9), .en(we), .Q(O9), .clk(clk), .clr(reset));
  Register #(.width(32)) register_7 (.D(I17), .en(we), .Q(O17), .clk(clk), .clr(reset));
  Register #(.width(32)) register_8 (.D(I25), .en(we), .Q(O25), .clk(clk), .clr(reset));
  Register #(.width(32)) register_9 (.D(I2), .en(we), .Q(O2), .clk(clk), .clr(reset));
  Register #(.width(32)) register_10 (.D(I10), .en(we), .Q(O10), .clk(clk), .clr(reset));
  Register #(.width(32)) register_11 (.D(I18), .en(we), .Q(O18), .clk(clk), .clr(reset));
  Register #(.width(32)) register_12 (.D(I26), .en(we), .Q(O26), .clk(clk), .clr(reset));
  Register #(.width(32)) register_13 (.D(I3), .en(we), .Q(O3), .clk(clk), .clr(reset));
  Register #(.width(32)) register_14 (.D(I11), .en(we), .Q(O11), .clk(clk), .clr(reset));
  Register #(.width(32)) register_15 (.D(I19), .en(we), .Q(O19), .clk(clk), .clr(reset));
  Register #(.width(32)) register_16 (.D(I27), .en(we), .Q(O27), .clk(clk), .clr(reset));
  Register #(.width(32)) register_17 (.D(I4), .en(we), .Q(O4), .clk(clk), .clr(reset));
  Register #(.width(32)) register_18 (.D(I12), .en(we), .Q(O12), .clk(clk), .clr(reset));
  Register #(.width(32)) register_19 (.D(I20), .en(we), .Q(O20), .clk(clk), .clr(reset));
  Register #(.width(32)) register_20 (.D(I28), .en(we), .Q(O28), .clk(clk), .clr(reset));
  Register #(.width(32)) register_21 (.D(I5), .en(we), .Q(O5), .clk(clk), .clr(reset));
  Register #(.width(32)) register_22 (.D(I13), .en(we), .Q(O13), .clk(clk), .clr(reset));
  Register #(.width(32)) register_23 (.D(I21), .en(we), .Q(O21), .clk(clk), .clr(reset));
  Register #(.width(32)) register_24 (.D(I29), .en(we), .Q(O29), .clk(clk), .clr(reset));
  Register #(.width(32)) register_25 (.D(I6), .en(we), .Q(O6), .clk(clk), .clr(reset));
  Register #(.width(32)) register_26 (.D(I14), .en(we), .Q(O14), .clk(clk), .clr(reset));
  Register #(.width(32)) register_27 (.D(I22), .en(we), .Q(O22), .clk(clk), .clr(reset));
  Register #(.width(32)) register_28 (.D(I30), .en(we), .Q(O30), .clk(clk), .clr(reset));
  Register #(.width(32)) register_29 (.D(I7), .en(we), .Q(O7), .clk(clk), .clr(reset));
  Register #(.width(32)) register_30 (.D(I15), .en(we), .Q(O15), .clk(clk), .clr(reset));
  Register #(.width(32)) register_31 (.D(I23), .en(we), .Q(O23), .clk(clk), .clr(reset));
  Register #(.width(32)) register_32 (.D(I31), .en(we), .Q(O31), .clk(clk), .clr(reset));
endmodule
